# Fritzing sketch Arduino simple weather station sketch (saved by Fritzing 1.0.6)
breadboards: 1

parts:
  Part1 = Arduino Uno (Rev3)
  Part2 = Barometric Pressure Sensor - BMP180 Breakout (GY-68)
  M1 = MQ-135 Air Quality Sensor Module
  7_Segment1 = 7 Segment Display
  A1 = DHT22 module
  R1 = Resistor [tolerance=±5% power=0.25W resistance=220 package=THT]

nets:
  N1: Part1.A0, M1.AO
  N2: Part1.D8, 7_Segment1.Segment_D
  N3: Part1.D9_PWM, 7_Segment1.Segment_E
  N4: Part1.D10_PWM/SS, 7_Segment1.Segment_F
  N5: Part1.D11_PWM/MOSI, 7_Segment1.Segment_G
  GND: Part1.GND, Part2.GND, M1.GND, A1.-, R1.Pin_1
  N6: Part1.A4/SDA, Part2.SDA
  N7: Part1.A5/SCL, Part2.SCL
  N8: Part1.D2, A1.Out
  N9: Part1.D5_PWM, 7_Segment1.Segment_A
  N10: Part1.D6_PWM, 7_Segment1.Segment_B
  N11: Part1.D7, 7_Segment1.Segment_C
  3V3: Part1.3V3, Part2.VCC
  5V: Part1.5V, M1.VCC, A1.+
  N12: 7_Segment1.common_cathode, R1.Pin_0

custom parts:
  MQ-135 Air Quality Sensor Module: The MQ-135 air quality sensor is one of range of MQ gas sensors that can be used to detect, measure, and monitor a wide range of gases, including NH3, NOx, CO2, benzene, and smoke, present in the atmosphere.
  DHT22 module: DHT22 module. Pins VCC Data GND.
